// Logisim project ISA Projetos Digitais.circ as structural Verilog: 5 circuits, main circuit main
module main (
  input  in_1
);

  wire AndEq_out, AndLt_out, AndNe_out, Beq, Blt, Bne, CLK, JalR, Jump, MemWrite, not_1_out, or_1_out,
       RegWrite, SelMul, TipoR, TipoS, ULASrc, Zero;
  wire [0:0] SelPC;
  wire [1:0] ImmSrc, ResultSrc;
  wire [2:0] multiplexer_5_out, ULAOP;
  wire [3:0] B03, B4_7, B8_11, B12_15, B16_19, multiplexer_2_out;
  wire [11:0] EndMDEM;
  wire [19:0] A, adder_1_out, B, DadoBR, DadoMD, IMM, Mul, multiplexer_1_out, multiplexer_4_out, PC, PC_1,
       RFinal;
  wire [19:12] RULA;

  Clock u_clk (.out(CLK));
  Multiplexer #(.select(2), .width(20)) multiplexer_1 (
    .in0(PC_1), .in1(adder_1_out), .in2({RULA, EndMDEM}), .in3(PC_1), .out(multiplexer_1_out),
    .sel({JalR, SelPC[0]}));
  Register #(.width(20)) u_PC (.D(multiplexer_1_out), .clk(CLK), .Q(PC), .clr(in_1));  // open: en
  Adder #(.width(20)) adder_1 (.a(PC_1), .b(IMM), .out(adder_1_out));  // open: cin, cout
  Adder #(.width(20)) adder_2 (.a(PC), .b(20'h1), .out(PC_1));  // open: cin, cout
  Unidade_Controle unidade_controle_1 (
    .OPC(B16_19), .TipoR(TipoR), .TipoS(TipoS), .JalR(JalR), .Jump(Jump), .Blt(Blt), .Bne(Bne), .Beq(Beq),
    .ImmSrc(ImmSrc), .ResultSrc(ResultSrc), .MemWrite(MemWrite), .ULAOP(ULAOP), .ULASrc(ULASrc),
    .RegWrite(RegWrite));
  ROM #(.addrWidth(12), .dataWidth(20)) IMEM (.addr(PC[11:0]), .data({B16_19, B12_15, B8_11, B4_7, B03}));
  Multiplexer #(.width(4)) multiplexer_2 (.in0(B4_7), .in1(B12_15), .out(multiplexer_2_out), .sel(TipoS));
  Gerador_Imediato gerador_imediato_1 (.I({B16_19, B12_15, B8_11, B4_7, B03}), .SEL(ImmSrc), .IMM(IMM));
  Multiplexer #(.select(2), .width(20)) multiplexer_3 (
    .in0(RFinal), .in1(DadoMD), .in2(PC_1), .in3(RFinal), .out(DadoBR), .sel(ResultSrc));
  Banco_Registradores banco_registradores_1 (
    .D(DadoBR), .rd(B12_15), .rs1(B8_11), .rs2(multiplexer_2_out), .W(RegWrite), .clk(CLK), .A(A), .out_8(B));
  Multiplexer #(.width(20)) multiplexer_4 (.in0(B), .in1(IMM), .out(multiplexer_4_out), .sel(ULASrc));
  Multiplexer #(.width(3)) multiplexer_5 (.in0(ULAOP), .in1(B03[2:0]), .out(multiplexer_5_out), .sel(TipoR));
  and and_1 (SelMul, TipoR, B03[3]);
  Multiplier #(.width(20)) multiplier_1 (.a(A), .b(B), .out(Mul));  // open: cin, cout
  or SelLow (SelPC[0], Jump, or_1_out);
  ULA ula_1 (.A(A), .B(multiplexer_4_out), .OP(multiplexer_5_out), .R({RULA, EndMDEM}), .Zero(Zero));
  or or_1 (or_1_out, AndEq_out, AndNe_out, AndLt_out);
  and AndEq (AndEq_out, Beq, Zero);
  not not_1 (not_1_out, Zero);
  and AndNe (AndNe_out, not_1_out, Bne);
  and AndLt (AndLt_out, Blt, EndMDEM[0]);
  Multiplexer #(.width(20)) multiplexer_6 (.in0({RULA, EndMDEM}), .in1(Mul), .out(RFinal), .sel(SelMul));
  RAM #(.addrWidth(12), .asyncread("true"), .dataWidth(20)) ram_1 (
    .addr(EndMDEM), .we(MemWrite), .oe(1'b1), .clk(CLK), .din(B), .dout(DadoMD));

  // Other names for the same wires on the sheet: IMM2[19:0] = {B16_19, B12_15, B8_11, B4_7, B03};
  //   PC0_11[11:0] = PC[11:0]; RULA[11:0] = EndMDEM; SelPC[1] = JalR
endmodule

module Banco_Registradores (
  input  [19:0] D,
  input  [3:0] rd,
  input  [3:0] rs1,
  input  [3:0] rs2,
  input  W,
  input  clk,
  output [19:0] A,
  output [19:0] out_8
);

  wire Dx1, Dx2, Dx3, Dx4, Dx5, Dx6, Dx7, Dx8, Dx9, Dx10, Dx11, Dx12, Dx13, Dx14, Dx15;
  wire [19:0] Valorx1, Valorx2, Valorx3, Valorx4, Valorx5, Valorx6, Valorx7, Valorx8, Valorx9, Valorx10,
       Valorx11, Valorx12, Valorx13, Valorx14, Valorx15;

  Decoder #(.select(4)) decoder_1 (
    .out1(Dx1), .out2(Dx2), .out3(Dx3), .out4(Dx4), .out5(Dx5), .out6(Dx6), .out7(Dx7), .out8(Dx8),
    .out9(Dx9), .out10(Dx10), .out11(Dx11), .out12(Dx12), .out13(Dx13), .out14(Dx14), .out15(Dx15), .sel(rd),
    .en(W));  // open: out0
  Register #(.width(20)) a3_x7 (.D(D), .en(Dx7), .clk(clk), .Q(Valorx7));  // open: clr
  Register #(.width(20)) ra_x1 (.D(D), .en(Dx1), .clk(clk), .Q(Valorx1));  // open: clr
  Register #(.width(20)) sp_x2 (.D(D), .en(Dx2), .clk(clk), .Q(Valorx2));  // open: clr
  Register #(.width(20)) gp_x3 (.D(D), .en(Dx3), .clk(clk), .Q(Valorx3));  // open: clr
  Register #(.width(20)) a0_x4 (.D(D), .en(Dx4), .clk(clk), .Q(Valorx4));  // open: clr
  Register #(.width(20)) a1_x5 (.D(D), .en(Dx5), .clk(clk), .Q(Valorx5));  // open: clr
  Register #(.width(20)) a2_x6 (.D(D), .en(Dx6), .clk(clk), .Q(Valorx6));  // open: clr
  Register #(.width(20)) t0_x8 (.D(D), .en(Dx8), .clk(clk), .Q(Valorx8));  // open: clr
  Register #(.width(20)) s2_x14 (.D(D), .en(Dx14), .clk(clk), .Q(Valorx14));  // open: clr
  Register #(.width(20)) t1_x9 (.D(D), .en(Dx9), .clk(clk), .Q(Valorx9));  // open: clr
  Register #(.width(20)) t2_x10 (.D(D), .en(Dx10), .clk(clk), .Q(Valorx10));  // open: clr
  Register #(.width(20)) t3_x11 (.D(D), .en(Dx11), .clk(clk), .Q(Valorx11));  // open: clr
  Register #(.width(20)) s0_x12 (.D(D), .en(Dx12), .clk(clk), .Q(Valorx12));  // open: clr
  Register #(.width(20)) s1_x13 (.D(D), .en(Dx13), .clk(clk), .Q(Valorx13));  // open: clr
  Register #(.width(20)) s3_x15 (.D(D), .en(Dx15), .clk(clk), .Q(Valorx15));  // open: clr
  Multiplexer #(.select(4), .width(20)) multiplexer_1 (
    .in0({20{1'b0}}), .in1(Valorx1), .in2(Valorx2), .in3(Valorx3), .in4(Valorx4), .in5(Valorx5),
    .in6(Valorx6), .in7(Valorx7), .in8(Valorx8), .in9(Valorx9), .in10(Valorx10), .in11(Valorx11),
    .in12(Valorx12), .in13(Valorx13), .in14(Valorx14), .in15(Valorx15), .out(A), .sel(rs1));
  Multiplexer #(.select(4), .width(20)) multiplexer_2 (
    .in0({20{1'b0}}), .in1(Valorx1), .in2(Valorx2), .in3(Valorx3), .in4(Valorx4), .in5(Valorx5),
    .in6(Valorx6), .in7(Valorx7), .in8(Valorx8), .in9(Valorx9), .in10(Valorx10), .in11(Valorx11),
    .in12(Valorx12), .in13(Valorx13), .in14(Valorx14), .in15(Valorx15), .out(out_8), .sel(rs2));

  // Other names for the same wires on the sheet: Dado[19:0] = D
endmodule

module ULA (
  input  [19:0] A,
  input  [19:0] B,
  input  [2:0] OP,
  output [19:0] R,
  output Zero
);

  wire comparator_1_lt;
  wire [19:0] adder_1_out, and_1_out, bit_extender_1_out, or_1_out, shifter_1_out, shifter_2_out,
       subtractor_1_out, xor_1_out;

  Adder #(.width(20)) adder_1 (.a(A), .b(B), .out(adder_1_out));  // open: cin, cout
  Subtractor #(.width(20)) subtractor_1 (.a(A), .b(B), .out(subtractor_1_out));  // open: bin, bout
  Comparator #(.width(20)) comparator_1 (.a(A), .b(B), .lt(comparator_1_lt));  // open: gt, eq
  Shifter #(.width(20)) shifter_1 (.in(A), .\dist (B[4:0]), .out(shifter_1_out));
  Shifter #(.shift("lr"), .width(20)) shifter_2 (.in(A), .\dist (B[4:0]), .out(shifter_2_out));
  assign and_1_out = A & B;  // AND_Gate and_1, 20 bits wide
  assign or_1_out = A | B;  // OR_Gate or_1, 20 bits wide
  assign xor_1_out = A ^ B;  // XOR_Gate xor_1, 20 bits wide
  assign bit_extender_1_out = {{19{1'b0}}, comparator_1_lt};  // Bit_Extender bit_extender_1
  Multiplexer #(.select(3), .width(20)) multiplexer_1 (
    .in0(adder_1_out), .in1(subtractor_1_out), .in2(and_1_out), .in3(or_1_out), .in4(xor_1_out),
    .in5(bit_extender_1_out), .in6(shifter_1_out), .in7(shifter_2_out), .out(R), .sel(OP));
  Comparator #(.width(20)) comparator_2 (.a(R), .b({20{1'b0}}), .eq(Zero));  // open: gt, lt
endmodule

module Gerador_Imediato (
  input  [19:0] I,
  input  [1:0] SEL,
  output [19:0] IMM
);

  wire [19:0] bit_extender_1_out, bit_extender_2_out, bit_extender_3_out;

  assign bit_extender_1_out = {{12{I[7]}}, I[7:0]};  // Bit_Extender bit_extender_1
  assign bit_extender_2_out = {{12{1'b0}}, I[7:0]};  // Bit_Extender bit_extender_2
  assign bit_extender_3_out = {{8{I[11]}}, I[11:0]};  // Bit_Extender bit_extender_3
  Multiplexer #(.select(2), .width(20)) multiplexer_1 (
    .in0(bit_extender_1_out), .in1(bit_extender_3_out), .in2(bit_extender_1_out), .in3(bit_extender_2_out),
    .out(IMM), .sel(SEL));
endmodule

module Unidade_Controle (
  input  [3:0] OPC,
  output TipoR,
  output TipoS,
  output JalR,
  output Jump,
  output Blt,
  output Bne,
  output Beq,
  output [1:0] ImmSrc,
  output [1:0] ResultSrc,
  output MemWrite,
  output [2:0] ULAOP,
  output ULASrc,
  output RegWrite
);

  ROM #(.addrWidth(4), .dataWidth(17)) rom_1 (
    .addr(OPC),
    .data({RegWrite, ULASrc, ULAOP, MemWrite, ResultSrc, ImmSrc, Beq, Bne, Blt, Jump, JalR, TipoS, TipoR}));

  // Notes on the sheet:
  //   contents of rom_1 (hex, n*v repeats v):
  //   10001 18000 1a180 1b180 18200 8802 1042 1022 5012 10488 18404
endmodule
